# Fritzing sketch ALARMA_PUERTA (saved by Fritzing 0.9.3b)
breadboards: 1

parts:
  Componente1 = Arduino Uno (Rev3)
  S1 = Reed switch [package=THT]
  LED1 = smd LED [color="Red (633nm)" package="0603 [SMD]"]
  R1 = Resistor [tolerance=±5% resistance=1k package=THT]
  R2 = Resistor [tolerance=±5% resistance=1k package=THT]

nets:
  N1: Componente1.D13/SCK, LED1.anode, R2.Pin_0
  N2: Componente1.D2, S1.pin_1, R1.Pin_1
  N3: Componente1.5V, R1.Pin_0, R2.Pin_1
  N4: Componente1.GND, S1.pin_2, LED1.cathode

// code stored in the sketch: Untitled2.ino

 
int contacto = 2;  //Pin asignado al reed switch
int led= 13;       //Pin asignado al LED
 

void setup() // Se ejecuta cada vez que el Arduino se inicia
{
  pinMode(contacto,INPUT); //El reed switch como una entrada
  pinMode(led, OUTPUT);    //El LED como una salida
 
}
 

void loop() 
{           
 
  // Si el iman se acerca al reed switch
  if (digitalRead(contacto)==HIGH){
 
    //Ciclo for que va de 0 a 50, el contador esta
    //  en la variable a, se repite mientras a sea
    //  menor a 50
    for(int a=0; a<50; a++){
 
      digitalWrite(led,HIGH); //Prende el LED
      delay(50); //Tiempo
      digitalWrite(led,LOW); //Apaga el LED
      delay(50); //Tiempo
 
    }
 
  // Si el iman esta lejos del reed switch
  }else{  
 
    digitalWrite(led,LOW); //Mantiene apagado el LED
 
  } 
}
